# Fritzing sketch doorLocker (saved by Fritzing 0.9.0b)
breadboards: 1

parts:
  IC1 = L293D [package=THT]
  VCC1 = Battery
  M1 = DC Motor
  Part1 = Arduino Uno (Rev3)
  Matrix_keypad1 = KEYPAD 4x4
  R1 = Resistor [tolerance=±5% resistance=220 package="1206 [SMD]"]
  R2 = Resistor [tolerance=±5% resistance=220 package="1206 [SMD]"]
  R3 = Resistor [tolerance=±5% resistance=220 package="1206 [SMD]"]
  LED2 = RGB LED (com. cathode, rbg) [package="5 mm [THT]"]
  S1 = Square Pushbutton
  J1 = Piezo Speaker

nets:
  N1: IC1.Enable_1, Part1.5V, S1.leg1
  N2: IC1.In_1, IC1.0V, VCC1.-, Part1.GND, R3.Pin_1, J1.pin1
  N3: IC1.Out_1_(_Controlled_by_Enable_1_), M1.pin_1
  N4: IC1.Out_2_(_Controlled_by_Enable_1_), M1.pin_2
  N5: IC1.In_2, Part1.D2
  N6: IC1.+Vmotor, VCC1.+
  N7: Part1.D8, Matrix_keypad1.col4
  N8: Part1.D9_PWM, Matrix_keypad1.row1
  N9: Part1.D10_PWM/SS, Matrix_keypad1.row2
  N10: Part1.D11_PWM/MOSI, Matrix_keypad1.row3
  N11: Part1.D12/MISO, Matrix_keypad1.row4
  N12: Part1.D13/SCK, S1.leg0
  N13: Part1.D3_PWM, R2.Pin_1
  N14: Part1.D4, R1.Pin_1
  N15: Part1.D5_PWM, Matrix_keypad1.col1
  N16: Part1.D6_PWM, Matrix_keypad1.col2
  N17: Part1.D7, Matrix_keypad1.col3
  N18: R1.Pin_0, LED2.red_anode
  N19: R2.Pin_0, LED2.blue_anode, J1.pin2
  N20: R3.Pin_0, LED2.green_anode

notes:
  Or an AC power supply.
  Solenoid
  Not using blue

custom parts:
  KEYPAD 4x4: Matrix keypad 16 buttons, 4 rows x 4 columns
